# Fritzing sketch ATTiny7segBitshift (saved by Fritzing 0.9.3b)
perfboards: 1

parts:
  7_Segment1 = 7 Segment Display
  U1 = 74HC595 SMD [package="SO16 [SMD]"]
  U2 = attiny85 [package=dip]
  R1 = Resistor [tolerance=±5% resistance=330 package=THT]
  RHT1 = Humidity and Temperature Sensor RHT03

nets:
  N1: 7_Segment1.Segment_E, U1.Q4
  N2: 7_Segment1.Segment_D, U1.Q3
  N3: 7_Segment1.common_anode, R1.Pin_0
  N4: 7_Segment1.Segment_C, U1.Q2
  N5: 7_Segment1.Segment_DP, U1.Q7
  N6: 7_Segment1.Segment_B, U1.Q1
  N7: 7_Segment1.Segment_A, U1.Q0
  N8: 7_Segment1.Segment_F, U1.Q5
  N9: 7_Segment1.Segment_G, U1.Q6
  N10: U1.MR, RHT1.Vcc
  N11: U1.SH_CP, U2.Pin_7
  N12: U1.ST_CP, U2.Pin_2
  N13: U1.OE, RHT1.GND_2
  N14: U1.DS, U2.Pin_3
  N15: U2.Pin_5, R1.Pin_1
  N16: U2.Pin_6, RHT1.Data-signal
